// Logisim project Circ1.circ as structural Verilog: 1 circuit, main circuit Primeiro
module Primeiro (
  input  A,
  input  B,
  input  C,
  output out_4
);

  wire and_1_out, Negado_out;

  and Negado (Negado_out, ~A, ~C);  // AND_Gate
  and and_1 (and_1_out, B, C);
  or or_1 (out_4, Negado_out, and_1_out);

  // Notes on the sheet:
  //   S = (A'.C') + (B.C)
  //   2^3 = 8 saídas
endmodule
